# Fritzing sketch diagram (saved by Fritzing 0.9.4)
circuit board: 7.51837cm x 4.71569cm
breadboards: 1

parts:
  WeMos_D1_Mini1 = WeMos D1 Mini
  U5 = Sharp PC817 [part_number=PC817XI package=SMT]
  U4 = Sharp PC817 [part_number=PC817XI package=SMT]
  U3 = Sharp PC817 [part_number=PC817XI package=SMT]
  R5 = Resistor [tolerance=±5% resistance=150 package=THT]
  R4 = Resistor [tolerance=±5% resistance=150 package=THT]
  R2 = Resistor [tolerance=±5% resistance=150 package=THT]
  R3 = Resistor [tolerance=±5% resistance=150 package=THT]
  hc-sr1 = hc-sr04
  U2 = Sharp PC817 [part_number=PC817XI package=SMT]
  J1 = Screw terminal - 2 pins [package=THT]  # not connected
  J2 = Screw terminal - 2 pins [package=THT]
  J3 = Screw terminal - 2 pins [package=THT]
  J4 = Screw terminal - 2 pins [package=THT]  # not connected
  J5 = Screw terminal - 2 pins [package=THT]
  J6 = Screw terminal - 2 pins [package=THT]
  J7 = Screw terminal - 2 pins [package=THT]  # not connected

nets:
  5V: WeMos_D1_Mini1.5V, hc-sr1.VCC
  N1: WeMos_D1_Mini1.D0, hc-sr1.Echo
  N2: WeMos_D1_Mini1.D2, hc-sr1.Trig
  N3: WeMos_D1_Mini1.D5, R5.Pin_0
  N4: WeMos_D1_Mini1.D6, R4.Pin_0
  N5: WeMos_D1_Mini1.D7, R2.Pin_0
  N6: WeMos_D1_Mini1.D8, R3.Pin_0
  N7: WeMos_D1_Mini1.G, U5.Pin_2, U4.Pin_2, U3.Pin_2, hc-sr1.GND, U2.Pin_2
  N8: U5.Pin_1, R5.Pin_1
  N9: U5.Pin_4, J5.pin2
  N10: U5.Pin_3, U4.Pin_3, U3.Pin_3, U2.Pin_3
  N11: U4.Pin_1, R4.Pin_1
  N12: U4.Pin_4, J6.pin2
  N13: U3.Pin_1, R3.Pin_1
  N14: U3.Pin_4, J2.pin2
  N15: R2.Pin_1, U2.Pin_1
  N16: U2.Pin_4, J3.pin2

notes:
  Forward Voltage: 1.2 (max 1.4V)
  20mA
  (5V – 1.2V) / 0.02A = 190Ω
  (5V – 1.4V) / 0.02A = 180Ω
  (3.3V – 1.2V) / 0.02A ) = 105Ω
  (3.3V – 1.4V) / 0.02A ) = 95Ω
  0V
  S3
  24V
  S5
  S4
  S2
